# Fritzing sketch FritzingSketch (saved by Fritzing 0.9.3b)
breadboards: 1

parts:
  Part1 = Arduino Xbee Libellium Shield
  U1 = XBEE-1 [package=xbee-1_lock]  # not connected
  Part2 = Arduino Uno (Rev3)  # not connected
  Part3 = Arduino Uno (Rev3)  # not connected
  Part4 = Arduino Xbee Libellium Shield
  U2 = XBEE-1 [package=xbee-1_lock]  # not connected
  Part5 = Arduino Uno (Rev3)  # not connected
  Part6 = Arduino Xbee Libellium Shield
  U3 = XBEE-1 [package=xbee-1_lock]  # not connected
  Part7 = Arduino Uno (Rev3)
  Part8 = Arduino Xbee Libellium Shield
  U4 = XBEE-1 [package=xbee-1_lock]  # not connected
  U5 = POT [package=pot_mammoth]
  U6 = POT [package=pot_mammoth]
  U7 = POT [package=pot_mammoth]
  LED1 = RGB LED - (4 legs) [package="5 mm [THT]"]

nets:
  N1: Part1.A0, U5.A
  N2: Part4.A0, U6.A
  N3: Part6.A0, U7.A
  N4: Part7.D9_PWM, LED1.red_cathode
  N5: Part7.D10_PWM/SS, LED1.green_cathode
  N6: Part7.D11_PWM/MOSI, LED1.blue_cathode
  N7: Part8.+5V, U5.E, U6.E, U7.E
  N8: Part8.GND, U5.S, U6.S, U7.S, LED1.common_anode

notes:
  PANID = 17
  XBee S2 (XB24-ZB)
  3 * ZigBee Router AT (v22A7)
  Encryption = FB0CAD01
  Destination Address = 0000
  ZigBee Coordinator AT (v20A7)
